// Logisim project Timer.circ as structural Verilog: 1 circuit, main circuit main
module main (
  input  Signal,
  input  Enable,
  input  Clock,
  output Feedback,
  output Status
);

  wire not_1_out, not_2_out, s_r_ff_1_q, undriven;

  S_R_Flip_Flop s_r_ff_1 (.S(Signal), .clk(Clock), .R(1'b0), .Q(s_r_ff_1_q), .reset(undriven));  // open: Qn, preset, en
  not not_1 (not_1_out, undriven);
  not not_2 (not_2_out, s_r_ff_1_q);
  and and_1 (Status, s_r_ff_1_q, not_1_out);
  D_Flip_Flop d_ff_1 (.clk(Enable), .D(Status), .Q(Feedback));  // open: Qn, preset, en, reset

  // Notes on the sheet:
  //   A circuit that combines the use of flip flop and counter to give feedback
  //   Counter
endmodule
