// Logisim project allot_doctor.circ as structural Verilog: 1 circuit, main circuit main
module main (
  input  A,
  input  B,
  input  S1_t,
  input  S2_t,
  input  in_5,
  output X,
  output Y,
  output ENABLE
);

  wire and_1_out, and_2_out, and_3_out, not_1_out, not_2_out, not_3_out, not_4_out, or_1_out, or_2_out;

  not not_1 (not_1_out, A);
  not not_2 (not_2_out, B);
  not not_3 (not_3_out, S1_t);
  not not_4 (not_4_out, S2_t);
  or or_1 (or_1_out, not_1_out, not_2_out);
  and and_1 (and_1_out, B, S1_t);
  and and_2 (and_2_out, S1_t, A);
  and and_3 (and_3_out, B, A);
  and and_4 (X, or_1_out, in_5, not_3_out);
  or or_2 (or_2_out, and_2_out, and_1_out, and_3_out);
  and and_5 (Y, or_2_out, in_5, not_4_out);

  assign ENABLE = in_5;

  // Notes on the sheet:
  //   ENABLE
  //   ALLOT_DOCTOR
endmodule
