// Logisim project allot_the_doctor .circ as structural Verilog: 5 circuits, main circuit main
module main (
  input  in_1,
  input  in_2,
  input  ENABLE,
  output out_4,
  output out_5,
  output out_6
);

  wire allot_doctor_1_enable, allot_doctor_1_x, allot_doctor_1_y, clock_1_out,
       doctor_availabilitystatus_1_out_5, doctor_availabilitystatus_1_out_6;

  allot_doctor allot_doctor_1 (
    .A(in_1), .B(in_2), .S1_t(doctor_availabilitystatus_1_out_6), .S2_t(doctor_availabilitystatus_1_out_5),
    .in_5(ENABLE), .X(allot_doctor_1_x), .Y(allot_doctor_1_y), .ENABLE(allot_doctor_1_enable));
  Clock clock_1 (.out(clock_1_out));
  doctor_availabilitystatus doctor_availabilitystatus_1 (
    .Y(allot_doctor_1_y), .X(allot_doctor_1_x), .Enable(allot_doctor_1_enable), .Clock(clock_1_out),
    .out_5(doctor_availabilitystatus_1_out_5), .out_6(doctor_availabilitystatus_1_out_6), .out_7(out_5),
    .out_8(out_4), .out_9(out_6));

  // Notes on the sheet:
  //   A
  //   B
  //   DOCTOR B
  //   DOCTOR A
  //   WAIT SIGNAL
endmodule

module allot_doctor (
  input  A,
  input  B,
  input  S1_t,
  input  S2_t,
  input  in_5,
  output X,
  output Y,
  output ENABLE
);

  wire and_1_out, and_2_out, and_3_out, not_1_out, not_2_out, not_3_out, not_4_out, or_1_out, or_2_out;

  not not_1 (not_1_out, A);
  not not_2 (not_2_out, B);
  not not_3 (not_3_out, S1_t);
  not not_4 (not_4_out, S2_t);
  or or_1 (or_1_out, not_1_out, not_2_out);
  and and_1 (and_1_out, B, S1_t);
  and and_2 (and_2_out, S1_t, A);
  and and_3 (and_3_out, B, A);
  and and_4 (X, or_1_out, in_5, not_3_out);
  or or_2 (or_2_out, and_2_out, and_1_out, and_3_out);
  and and_5 (Y, or_2_out, in_5, not_4_out);

  assign ENABLE = in_5;

  // Notes on the sheet:
  //   ENABLE
  //   ALLOT_DOCTOR
endmodule

module doctor_availabilitystatus (
  input  Y,
  input  X,
  input  Enable,
  input  Clock,
  output out_5,
  output out_6,
  output out_7,
  output out_8,
  output out_9
);

  wire and_2_out, and_3_out, not_1_out, not_2_out;

  not not_1 (not_1_out, Y);
  not not_2 (not_2_out, X);
  and and_1 (out_9, not_1_out, not_2_out);
  and and_2 (and_2_out, not_2_out, Y);
  and and_3 (and_3_out, X, not_1_out);
  timer timer_1 (.Signal(and_2_out), .Enable(Enable), .Clock(Clock), .Feedback(out_6), .Status(out_8));
  timer timer_2 (.Signal(and_3_out), .Enable(Enable), .Clock(Clock), .Feedback(out_5), .Status(out_7));

  // Notes on the sheet:
  //   INPUT EXPLANATION:
  //   X Y is input which reprsents the incoming query
  //   A
  //   During the consultation , the status of doctor availiability is kept occupied for 15 seconds
  //   DOTOR AVAILABILITY STATUS UPDATE
  //   Output explanation:
  //   The doctor availability status turns to 1
  //   Doctor status is further given as feedback and becomes input for allot_doctor
  //   WAIT REQUEST
  //   DOCTOR B STATUS UPDATE
  //   DOCTOR A STATUS UPDATE
  //   DOCTOR B STATUS
  //   DOCTOR A STATUS
endmodule

module timer (
  input  Signal,
  input  Enable,
  input  Clock,
  output Feedback,
  output Status
);

  wire counter_2_carry_is_1_when_counter_finishes, not_1_out, not_2_out, s_r_ff_1_q;

  Counter #(.width(4), .max('hf)) counter_1 ();  // open: load, D, count, Q, carry, clk, clr
  S_R_Flip_Flop s_r_ff_1 (
    .S(Signal), .clk(Clock), .R(1'b0), .Q(s_r_ff_1_q), .reset(counter_2_carry_is_1_when_counter_finishes));  // open: Qn, preset, en
  counter counter_2 (
    .Carry_is_1_when_counter_finishes(counter_2_carry_is_1_when_counter_finishes), .Clock(Clock),
    .Reset(not_2_out));
  not not_1 (not_1_out, counter_2_carry_is_1_when_counter_finishes);
  not not_2 (not_2_out, s_r_ff_1_q);
  and and_1 (Status, s_r_ff_1_q, not_1_out);
  D_Flip_Flop d_ff_1 (.clk(Enable), .D(Status), .Q(Feedback));  // open: Qn, preset, en, reset

  // Notes on the sheet:
  //   Timer
  //   A circuit that combines the use of flip flop and counter to give feedback
endmodule

module counter (
  input  Clock,
  input  Reset,
  output Carry_is_1_when_counter_finishes
);

  wire and_1_out, not_1_out;
  wire [3:0] t_ff_1_q;

  and and_1 (and_1_out, not_1_out, Clock);
  not not_1 (not_1_out, Carry_is_1_when_counter_finishes);
  T_Flip_Flop t_ff_1 (.clk(and_1_out), .T(1'b1), .Q(t_ff_1_q[0]), .reset(Reset), .en(1'b1));  // open: Qn, preset
  and and_2 (Carry_is_1_when_counter_finishes, t_ff_1_q[3], t_ff_1_q[2]);
  T_Flip_Flop #(.trigger("falling")) t_ff_2 (
    .clk(t_ff_1_q[0]), .T(1'b1), .Q(t_ff_1_q[1]), .reset(Reset), .en(1'b1));  // open: Qn, preset
  T_Flip_Flop #(.trigger("falling")) t_ff_3 (
    .clk(t_ff_1_q[1]), .T(1'b1), .Q(t_ff_1_q[2]), .reset(Reset), .en(1'b1));  // open: Qn, preset
  // Probe on t_ff_1_q
  T_Flip_Flop #(.trigger("falling")) t_ff_4 (
    .clk(t_ff_1_q[2]), .T(1'b1), .Q(t_ff_1_q[3]), .reset(Reset), .en(1'b1));  // open: Qn, preset

  // Notes on the sheet:
  //   Asynchronous counter circuit that stops counting as soon as it reaches the 0xD
  //   4 bit up counter
endmodule
