// Logisim project doctor_avaliable.circ as structural Verilog: 1 circuit, main circuit main
module main (
  input  Y,
  input  X,
  input  Enable,
  input  Clock,
  output out_5,
  output out_6,
  output out_7,
  output out_8,
  output out_9
);

  wire and_2_out, and_3_out, not_1_out, not_2_out;

  not not_1 (not_1_out, Y);
  not not_2 (not_2_out, X);
  and and_1 (out_9, not_1_out, not_2_out);
  and and_2 (and_2_out, not_2_out, Y);
  and and_3 (and_3_out, X, not_1_out);

  // Notes on the sheet:
  //   INPUT EXPLANATION:
  //   X Y is input which reprsents the incoming query
  //   A
  //   Timer
  //   During the consultation , the status of doctor availiability is kept occupied for 15 seconds
  //   DOTOR AVAILABILITY STATUS UPDATE
  //   Timer
  //   Output explanation:
  //   The doctor availability status turns to 1
  //   Doctor status is further given as feedback and becomes input for allot_doctor
  //   WAIT REQUEST
  //   DOCTOR B STATUS UPDATE
  //   DOCTOR A STATUS UPDATE
  //   DOCTOR B STATUS
  //   DOCTOR A STATUS
endmodule
