// Logisim project main.circ as structural Verilog: 1 circuit, main circuit main
module main (
  input  in_1,
  input  in_2,
  input  ENABLE,
  output out_4,
  output out_5,
  output out_6
);

  wire clock_1_out;

  Clock clock_1 (.out(clock_1_out));

  // Notes on the sheet:
  //   A
  //   B
  //   Allot_doctor
  //   doctor_avaliability
  //   DOCTOR B
  //   DOCTOR A
  //   WAIT SIGNAL
endmodule
